// Digital circuit ID.dig as structural Verilog
module ID (
);

  fb_imm_gen #(.applicationType("IVERILOG"), .iverilogOptions("-I /Users/zhangyibo/riscvdesign/RISCVFirebird/AssemblyLine/rtl\n-y/Users/zhangyibo/riscvdesign/RISCVFirebird/AssemblyLine/rtl"), .CodeFile("/Users/zhangyibo/riscvdesign/RISCVFirebird/AssemblyLine/rtl/fb_imm_gen.v")) u_fb_imm_gen ();  // open: inst, imm
endmodule
