// Digital circuit IF.dig as structural Verilog
module IF (
  input  PC1,
  input  _1,
  input  _2,
  output [31:0] _444
);

  wire _3_c_o;
  wire [31:0] _3_s, u_fb_pc_out_address;

  fb_pc #(.applicationType("IVERILOG"), .iverilogOptions("-y /Users/zhangyibo/riscvdesign/RISCVFirebird/AssemblyLine/rtl\n-I /Users/zhangyibo/riscvdesign/RISCVFirebird/AssemblyLine/rtl"), .CodeFile("/Users/zhangyibo/riscvdesign/RISCVFirebird/AssemblyLine/rtl/fb_pc.v")) u_fb_pc (
    .pc_write(_1), .clk(PC1), .pc_reset(_2), .new_address(_3_s), .out_address(u_fb_pc_out_address));
  Add #(.Bits(32)) _3 (.a(u_fb_pc_out_address), .b(32'h1), .c_i(_3_c_o), .s(_3_s), .c_o(_3_c_o));
  ROM #(.AddrBits(10), .Bits(32)) instmem (.A(u_fb_pc_out_address[9:0]), .sel(1'b1), .D(_444));
  // Pins of 10 and 32 bits meet at u_fb_pc_out_address
  // Pins of 1 and 32 bits meet at _444
  // also tied to GND on the sheet: _3_c_o

  // Notes on the sheet:
  //   _2: 2
endmodule
