// Digital circuit IFIDReg.dig as structural Verilog
module IFIDReg (
  input  clk,
  input  lk,
  input  we,
  input  [31:0] pc,
  input  [31:0] ir,
  output [31:0] opc,
  output [31:0] oir
);

  fb_ifidreg #(.applicationType("IVERILOG"), .iverilogOptions("-y /Users/zhangyibo/riscvdesign/RISCVFirebird/AssemblyLine/rtl \n-I /Users/zhangyibo/riscvdesign/RISCVFirebird/AssemblyLine/rtl"), .CodeFile("/Users/zhangyibo/riscvdesign/RISCVFirebird/AssemblyLine/rtl/fb_ifidreg.v")) u_fb_ifidreg (
    .clk(clk), .lock(lk), .we(we), .if_pc(pc), .if_inst(ir), .id_pc(opc), .id_inst(oir));

  // Notes on the sheet:
  //   lk: 锁定当前寄存器的控制信号
  //   we: 写使能信号
  //   pc: pc 指令地址
  //   ir: 指令
  //   opc: pc 指令地址
  //   oir: 指令
endmodule

/* Test case test:
clk lk we pc ir opc oir
0 0 1 1 1 0 0
C 0 1 1 1 1 1
0 1 1 0 0 1 1
C 1 1 1 1 1 1
*/
