// Digital circuit EXMEMReg.dig as structural Verilog
module EXMEMReg (
  input  clk,
  input  we,
  input  rst,
  input  e1,
  input  e2,
  input  e3,
  input  e4,
  input  e5,
  input  [31:0] e6,
  input  [31:0] e7,
  input  [4:0] e8,
  input  [31:0] e10,
  input  [31:0] e9,
  input  [5:0] e11,
  input  [31:0] e12,
  output m1,
  output m2,
  output m3,
  output m4,
  output m5,
  output [31:0] m6,
  output [31:0] m7,
  output [4:0] m8,
  output [31:0] m9,
  output [31:0] m10,
  output [5:0] m11,
  output [31:0] m12
);

  fb_exmemreg #(.applicationType("IVERILOG"), .iverilogOptions("-y /Users/zhangyibo/riscvdesign/RISCVFirebird/Pipeline/rtl \n-I /Users/zhangyibo/riscvdesign/RISCVFirebird/Pipeline/rtl"), .CodeFile("/Users/zhangyibo/riscvdesign/RISCVFirebird/Pipeline/rtl/fb_exmemreg.v")) u_fb_exmemreg (
    .clk(clk), .we(we), .rst(rst), .ex_mem_read(e1), .ex_mem_write(e2), .ex_branch(e3), .ex_mem_to_reg(e4),
    .ex_reg_write(e5), .ex_alu_res(e6), .ex_rs2_data(e7), .ex_register_rd(e8), .ex_pc(e9), .ex_imm(e10),
    .ex_bra_control(e11), .ex_inst(e12), .mem_mem_read(m1), .mem_mem_write(m2), .mem_branch(m3),
    .mem_mem_to_reg(m4), .mem_reg_write(m5), .mem_alu_res(m6), .mem_rs2_data(m7), .mem_register_rd(m8),
    .mem_pc(m9), .mem_imm(m10), .mem_bra_control(m11), .mem_inst(m12));

  // Notes on the sheet:
  //   we: 写使能
  //   rst: 重置信号
  //   e1: 存储器读
  //   e2: 存储器写
  //   e3: 1 -> 表示这是一个B类型分支指令
  //   e4: mem_to_reg写回阶段使用:
  //   1 -> 寄存器写数值来源为memory
  //   0 -> 寄存器写数值来源为alu
  //   e5: 寄存器写使能
  //   e6: alu计算结果：可能是alu 或者 pc + 1(jalr)
  //   e7: 寄存器2中读取到的数据(rs2 data)
  //   e8: 目的寄存器编号，用于前递单元
  //   m1: 存储器读
  //   m2: 存储器写
  //   m3: 1 -> 表示这是一个B类型分支指令
  //   m4: mem_to_reg写回阶段使用:
  //   1 -> 寄存器写数值来源为memory
  //   0 -> 寄存器写数值来源为alu
  //   m5: 寄存器写使能
  //   m6: alu计算结果：可能是alu 或者 pc + 1(jalr)
  //   m7: 寄存器2中读取到的数据(rs2 data)
  //   m8: 目的寄存器编号，用于前递单元
  //   e10: ex阶段传来的imm,用于branch
  //   e9: ex阶段传来的pc，用于branch
  //   e11: ex阶段传来的bra控制信号
  //   m9: ex阶段传来的pc，用于branch
  //   m10: ex阶段传来的imm,用于branch
  //   m11: ex阶段传来的bra控制信号
  //   e12: 指令
  //   m12: 指令
endmodule
