// Digital circuit ID.dig as structural Verilog
module ID (
);

  fb_hazard_detection_unit #(.applicationType("IVERILOG"), .iverilogOptions("-I /Users/zhangyibo/riscvdesign/RISCVFirebird/Pipeline/rtl\n-y/Users/zhangyibo/riscvdesign/RISCVFirebird/Pipeline/rtl"), .CodeFile("/Users/zhangyibo/riscvdesign/RISCVFirebird/Pipeline/rtl/fb_hazard_detection_unit.v")) u_fb_hazard_detection_unit ();  // open: id_ex_memread, id_ex_register_rd, inst, lock
  fb_imm_gen #(.applicationType("IVERILOG"), .iverilogOptions("-I /Users/zhangyibo/riscvdesign/RISCVFirebird/Pipeline/rtl\n-y/Users/zhangyibo/riscvdesign/RISCVFirebird/Pipeline/rtl"), .CodeFile("/Users/zhangyibo/riscvdesign/RISCVFirebird/Pipeline/rtl/fb_imm_gen.v")) u_fb_imm_gen ();  // open: inst, imm
  fb_cu #(.applicationType("IVERILOG"), .iverilogOptions("-I /Users/zhangyibo/riscvdesign/RISCVFirebird/Pipeline/rtl\n-y/Users/zhangyibo/riscvdesign/RISCVFirebird/Pipeline/rtl"), .CodeFile("/Users/zhangyibo/riscvdesign/RISCVFirebird/Pipeline/rtl/fb_cu.v")) u_fb_cu ();  // open: opcode, alu_op, alu_src, alu_res_src, mem_read, mem_write, branch, mem_to_reg, reg_write
endmodule
