// Digital circuit IDEXReg.dig as structural Verilog
module IDEXReg (
  input  clk,
  input  we,
  input  rst,
  input  i1,
  input  i2,
  input  i3,
  input  i4,
  input  i5,
  input  i6,
  input  i7,
  input  [31:0] i8,
  input  [31:0] i9,
  input  [31:0] i10,
  input  [31:0] i11,
  input  [4:0] i12,
  input  [4:0] i13,
  input  [4:0] i14,
  input  [18:0] i15,
  input  lk,
  input  [31:0] i16,
  input  [5:0] i17,
  input  [31:0] i18,
  output e1,
  output e2,
  output e3,
  output e4,
  output e5,
  output e6,
  output e7,
  output [31:0] e8,
  output [31:0] e9,
  output [31:0] e10,
  output [31:0] e11,
  output [4:0] e12,
  output [4:0] e13,
  output [4:0] e14,
  output [18:0] e15,
  output [5:0] e17,
  output [31:0] e16,
  output [31:0] e18
);

  fb_idexreg #(.applicationType("IVERILOG"), .iverilogOptions("-I /Users/zhangyibo/riscvdesign/RISCVFirebird/Pipeline/rtl\n-y/Users/zhangyibo/riscvdesign/RISCVFirebird/Pipeline/rtl"), .CodeFile("/Users/zhangyibo/riscvdesign/RISCVFirebird/Pipeline/rtl/fb_idexreg.v")) u_fb_idexreg (
    .clk(clk), .we(we), .rst(rst), .id_alu_src(i1), .id_alu_res_src(i2), .id_mem_read(i3), .id_mem_write(i4),
    .id_branch(i5), .id_mem_to_reg(i6), .id_reg_write(i7), .id_pc_add_1(i8), .id_rs1_data(i9),
    .id_rs2_data(i10), .id_imm(i11), .id_register_rs1(i12), .id_register_rs2(i13), .id_register_rd(i14),
    .id_alu_control(i15), .lock(lk), .id_pc(i16), .id_bra_control(i17), .id_inst(i18), .ex_alu_src(e1),
    .ex_alu_res_src(e2), .ex_mem_read(e3), .ex_mem_write(e4), .ex_branch(e5), .ex_mem_to_reg(e6),
    .ex_reg_write(e7), .ex_pc_add_1(e8), .ex_rs1_data(e9), .ex_rs2_data(e10), .ex_imm(e11),
    .ex_register_rs1(e12), .ex_register_rs2(e13), .ex_register_rd(e14), .ex_alu_control(e15), .ex_pc(e16),
    .ex_bra_control(e17), .ex_inst(e18));
  // Pins of 1 and 32 bits meet at i8
  // Pins of 1 and 5 bits meet at i12
  // Pins of 1 and 5 bits meet at i13
  // Pins of 1 and 5 bits meet at i14
  // Pins of 1 and 32 bits meet at e8

  // Notes on the sheet:
  //   we: 写使能
  //   rst: 重置信号，出现控制冒险时重置
  //   i1: alusrc:alu其中一个数据源源于rs2或是立即数
  //   0 -> rs2
  //   1 -> 立即数
  //   i2: alu计算得到结果后的多路选择器
  //   用于jalr
  //   0 -> alu result
  //   1 -> pc + 1(jalr)
  //   i3: 访存读使能
  //   i4: 访存写使能
  //   i5: 1 -> 表示该指令是分支指令
  //   i6: mem_to_reg寄存器数据来源
  //   0 -> 来自alu计算结果
  //   1 -> 来自访存的数据
  //   i7: 寄存器写使能
  //   i8: pc + 1 jalr
  //   i9: rs1数据
  //   i10: rs2数据
  //   i11: 立即数
  //   i12: rs1寄存器号
  //   i13: rs2寄存器号
  //   i14: rd寄存器号
  //   i15: alu控制信号
  //   e1: alusrc:alu其中一个数据源源于rs2或是立即数
  //   0 -> rs2
  //   1 -> 立即数
  //   e2: alu计算得到结果后的多路选择器
  //   用于jalr
  //   0 -> alu result
  //   1 -> pc + 1(jalr)
  //   e3: 访存读使能
  //   e4: 访存写使能
  //   e5: 1 -> 表示该指令是分支指令
  //   e6: mem_to_reg寄存器数据来源
  //   0 -> 来自alu计算结果
  //   1 -> 来自访存的数据
  //   e7: 寄存器写使能
  //   e8: pc + 1 jalr
  //   e9: rs1数据
  //   e10: rs2数据
  //   e11: 立即数
  //   e12: rs1寄存器号
  //   e13: rs2寄存器号
  //   e14: rd寄存器号
  //   e15: alu控制信号
  //   lk: 流水线停顿信号
  //   i16: id阶段的pc，用于branch
  //   i17: branch控制信号
  //   e17: branch控制信号
  //   e16: id阶段传过来的pc，用于branch
  //   i18: 指令
  //   e18: 指令
endmodule
