// Digital circuit IF.dig as structural Verilog
module IF (
  input  clk,
  input  pw,
  input  rs,
  input  [31:0] ad,
  input  clr,
  output [31:0] ir,
  output [31:0] pc
);

  wire u_fb_pc_clear_inst;
  wire [31:0] instmem_d;

  fb_pc #(.applicationType("IVERILOG"), .iverilogOptions("-y /Users/zhangyibo/riscvdesign/RISCVFirebird/Pipeline/rtl\n-I /Users/zhangyibo/riscvdesign/RISCVFirebird/Pipeline/rtl"), .CodeFile("/Users/zhangyibo/riscvdesign/RISCVFirebird/Pipeline/rtl/fb_pc.v")) u_fb_pc (
    .pc_write(pw), .clk(clk), .pc_reset(rs), .new_address(ad), .pc_clear(clr), .out_address(pc),
    .clear_inst(u_fb_pc_clear_inst));
  ROM #(.AddrBits(10), .Bits(32)) instmem (.A(pc[9:0]), .sel(1'b1), .D(instmem_d));
  Multiplexer #(.Bits(32)) multiplexer_1 (.sel(u_fb_pc_clear_inst), .in_0(instmem_d), .in_1({32{1'b0}}), .out(ir));

  // Notes on the sheet:
  //   clk: pin 2
  //   pw: 用于在插入气泡的时候锁住pc, pin 1
  //   rs: 用于重置pc, pin 3
  //   ir: 输出是指令寄存器中取出的指令, pin 6
  //   ad: 输入的32位pc新地址
  //   来源包括：pc自增或是分支指令的目的地址, pin 4
  //   pc: pc寄存器的数值, pin 7
  //   clr: 用于jalr产生的一周期暂停, pin 5
  //   contents of instmem (hex, n*v repeats v):
  //   100413,3000493,a00a13,913,100993,13,40002283,fe829ee3,40102283
  //   ,28f93,409282b3,28663,fff28293,13903b3,98913,38993,ff7ff06f,c93
  //   ,d13,90663,34963b3,3494933,7d2023,1d0d13,ff7ff06f,d00393,40702123
  //   ,6600393,40702123,6900393,40702123,6200393,40702123,6f00393,40702123
  //   ,6e00393,40702123,6100393,40702123,6300393,40702123,2800393,40702123
  //   ,41f02123,2900393,40702123,3d00393,40702123,19d0663,fffd0d13,d2383
  //   ,9383b3,40702123,ff7ff06f,d00393,40702123,febff06f
endmodule
