// Digital circuit IFIDReg.dig as structural Verilog
module IFIDReg (
  input  clk,
  input  lk,
  input  we,
  input  [31:0] pc,
  input  [31:0] ir,
  input  rst,
  input  [31:0] pcn,
  input  [5:0] iac,
  output [31:0] opc,
  output [31:0] oir,
  output [31:0] pn,
  output [5:0] oac
);

  fb_ifidreg #(.applicationType("IVERILOG"), .iverilogOptions("-y /Users/zhangyibo/riscvdesign/RISCVFirebird/Pipeline/rtl \n-I /Users/zhangyibo/riscvdesign/RISCVFirebird/Pipeline/rtl"), .CodeFile("/Users/zhangyibo/riscvdesign/RISCVFirebird/Pipeline/rtl/fb_ifidreg.v")) u_fb_ifidreg (
    .clk(clk), .lock(lk), .we(we), .rst(rst), .if_pc(pc), .if_pc_add_1(pcn), .if_inst(ir),
    .in_bra_control(iac), .id_pc(opc), .id_inst(oir), .id_pc_add_1(pn), .out_bra_control(oac));

  // Notes on the sheet:
  //   lk: 锁定当前寄存器的控制信号
  //   we: 写使能信号
  //   pc: pc 指令地址
  //   ir: 指令
  //   opc: pc 指令地址
  //   oir: 指令
  //   rst: rst清除信号，产生控制冒险时清空寄存器数据
  //   pcn: pcn 顺序执行下一指令地址，用于jalr指令
  //   pn: pn 下一指令地址，用于jalr指令
  //   iac: 输入的bra_control
  //   oac: 前面阶段传来的bra_control
endmodule

/* Test case test:
clk lk we pc ir opc oir
0 0 1 1 1 0 0
C 0 1 1 1 1 1
0 1 1 0 0 1 1
C 1 1 1 1 1 1
*/
