// Digital circuit MEMWBReg.dig as structural Verilog
module MEMWBReg (
  input  clk,
  input  we,
  input  m1,
  input  m2,
  input  [31:0] m3,
  input  [31:0] m4,
  input  [4:0] m5,
  input  [31:0] m6,
  output w1,
  output w2,
  output [31:0] w3,
  output [31:0] w4,
  output [4:0] w5,
  output [31:0] w6
);

  fb_memwbreg #(.applicationType("IVERILOG"), .iverilogOptions("-y /Users/zhangyibo/riscvdesign/RISCVFirebird/Pipeline/rtl \n-I /Users/zhangyibo/riscvdesign/RISCVFirebird/Pipeline/rtl"), .CodeFile("/Users/zhangyibo/riscvdesign/RISCVFirebird/Pipeline/rtl/fb_memwbreg.v")) u_fb_memwbreg (
    .clk(clk), .we(we), .mem_mem_to_reg(m1), .mem_reg_write(m2), .mem_memory_data(m3), .mem_alu_res(m4),
    .mem_register_rd(m5), .mem_inst(m6), .wb_mem_to_reg(w1), .wb_reg_write(w2), .wb_memory_data(w3),
    .wb_alu_res(w4), .wb_register_rd(w5), .wb_inst(w6));

  // Notes on the sheet:
  //   we: 写使能
  //   m1: mem_mem_to_reg:
  //   0 -> 寄存器写数据输入来自alu
  //   1 -> 寄存器写数据输入来自mem
  //   m2: mem_reg_write:寄存器写使能信号
  //   m3: mem_memory_data:从memory中读取出的值
  //   m4: mem_alu_res:在EX阶段alu计算出的数值
  //   m5: mem_register_rd:前面阶段传入的rd寄存器号
  //   w1: wb_mem_to_reg:
  //   0 -> 寄存器写数据输入来自alu
  //   1 -> 寄存器写数据输入来自mem
  //   w2: wb_reg_write:寄存器写使能信号
  //   w3: wb_memory_data:从memory中读取出的值
  //   w4: wb_alu_res:在EX阶段alu计算出的数值
  //   w5: wb_register_rd:前面阶段传入的rd寄存器号
  //   m6: 指令
  //   w6: 指令
endmodule
