// Digital circuit ROOT.dig as structural Verilog
module ROOT (
  input  _1,
  input  _0,
  input  clk,
  input  keyclk
);

  wire addsrc, alusrc, alusrc1, arsrc, bra, bra1, CF, clrstat, cthulk, dahulk, e00, e01, e2, e11, embra,
       emmr, emmtr, emmw, emrw, iibrac, jalren, keyboard_av, mr, mr1, mtr, mtr1, mw, mw1, mwmtr, mwrw, NF,
       opc, or_1_out, pca1, pcsrc, rst, rw, rw1, u_fb_alu_csr_write, u_t_f_decode_e10, VF, ZF;
  wire [1:0] aluop, fa, fb, u_fb_mmu_data_src;
  wire [3:0] u_fb_alu_csr;
  wire [4:0] emrd, mwrd, rdd, rs11, rs22;
  wire [5:0] embrac, iebrac, obrac;
  wire [9:0] mmuadd;
  wire [15:0] keyboard_d;
  wire [18:0] aluct, u_fb_alu_ctrl_alu_control;
  wire [31:0] bitextender_1_out, eddatareg_q, emalur, emimm, empc, emrs2d, errpc, fb_fwdmux_1_d,
       fb_fwdmux_2_d, idexreg_1_p30, idexreg_1_p31, iepc, ifinst, imm, immj, inst, mem_d, memwbreg_1_w3,
       memwbreg_1_w4, multiplexer_1_out, multiplexer_2_out, multiplexer_3_out, multiplexer_5_out,
       multiplexer_6_out, pc, pca11, pcn, rbval, succpc, u_fb_alu_alu_res, u_fb_regfile_rdata1,
       u_fb_regfile_rdata2, u_fb_status_reg_status, u_t_data_sel_data;

  fb_mmu #(.applicationType("IVERILOG"), .iverilogOptions("-I /Users/zhangyibo/riscvdesign/RISCVFirebird/Pipeline/rtl\n-y/Users/zhangyibo/riscvdesign/RISCVFirebird/Pipeline/rtl"), .CodeFile("/Users/zhangyibo/riscvdesign/RISCVFirebird/Pipeline/rtl/fb_mmu.v")) u_fb_mmu (
    .in_add(emalur[10:0]), .data_src(u_fb_mmu_data_src), .out_add(mmuadd), .clr_stat(clrstat));
  Keyboard keyboard (.C(clk), .en(_1), .D(keyboard_d), .av(keyboard_av));
  BitExtender #(.inputBits(16), .outputBits(32)) bitextender_1 (.in(keyboard_d), .out(bitextender_1_out));
  Multiplexer #(.Bits(32)) multiplexer_1 (.sel(addsrc), .in_0(succpc), .in_1(errpc), .out(multiplexer_1_out));
  t_f_decode #(.applicationType("IVERILOG"), .CodeFile("/Users/zhangyibo/riscvdesign/RISCVFirebird/Pipeline/rtl/t_f_decode.v")) u_t_f_decode (
    .c(u_fb_mmu_data_src), .e00(e00), .e01(e01), .e10(u_t_f_decode_e10), .e11(e11));
  Multiplexer #(.Bits(32)) multiplexer_2 (.sel(pcsrc), .in_0(pcn), .in_1(multiplexer_1_out), .out(multiplexer_2_out));
  Multiplexer #(.Bits(32)) multiplexer_3 (
    .sel(u_t_f_decode_e10), .in_0(bitextender_1_out), .in_1(emrs2d), .out(multiplexer_3_out));
  IF if_1 (.clk(clk), .pw(dahulk), .rs(_0), .ad(multiplexer_2_out), .clr(cthulk), .ir(ifinst), .pc(pc));
  or or_1 (or_1_out, u_t_f_decode_e10, keyboard_av);
  Add #(.Bits(32)) adderpc (.a(pc), .b(32'h1), .c_i(_0), .s(pcn), .c_o(_0));
  fb_status_reg #(.applicationType("IVERILOG"), .iverilogOptions("-I /Users/zhangyibo/riscvdesign/RISCVFirebird/Pipeline/rtl\n-y/Users/zhangyibo/riscvdesign/RISCVFirebird/Pipeline/rtl"), .CodeFile("/Users/zhangyibo/riscvdesign/RISCVFirebird/Pipeline/rtl/fb_status_reg.v")) u_fb_status_reg (
    .clk(clk), .clr(clrstat), .av(keyboard_av), .status(u_fb_status_reg_status));
  Register #(.Bits(32)) eddatareg (.D(bitextender_1_out), .C(clk), .en(keyboard_av), .Q(eddatareg_q));
  Terminal terminal (.D(multiplexer_3_out), .C(clk), .en(or_1_out));
  // IFIDReg ifidreg_1: pin names not known; wires that end beside it: clk, dahulk, _1, rst, pc, pcn, ifinst, obrac, opc, inst, pca1, iibrac
  RAMDualPort #(.AddrBits(10), .Bits(32)) mem (.A(mmuadd), .Din(emrs2d), .str(emmw), .C(clk), .ld(emmr), .D(mem_d));
  fb_hazard_detection_unit #(.applicationType("IVERILOG"), .iverilogOptions("-I /Users/zhangyibo/riscvdesign/RISCVFirebird/Pipeline/rtl\n-y/Users/zhangyibo/riscvdesign/RISCVFirebird/Pipeline/rtl"), .CodeFile("/Users/zhangyibo/riscvdesign/RISCVFirebird/Pipeline/rtl/fb_hazard_detection_unit.v")) u_fb_hazard_detection_unit (
    .id_ex_memread(mr1), .id_ex_register_rd(rdd), .inst(inst[24:15]), .lock(dahulk));
  fb_cu #(.applicationType("IVERILOG"), .iverilogOptions("-I /Users/zhangyibo/riscvdesign/RISCVFirebird/Pipeline/rtl\n-y/Users/zhangyibo/riscvdesign/RISCVFirebird/Pipeline/rtl"), .CodeFile("/Users/zhangyibo/riscvdesign/RISCVFirebird/Pipeline/rtl/fb_cu.v")) u_fb_cu (
    .opcode(inst[6:0]), .alu_op(aluop), .alu_src(alusrc), .alu_res_src(arsrc), .mem_read(mr), .mem_write(mw),
    .branch(bra), .mem_to_reg(mtr), .reg_write(rw), .jalr_en(jalren));
  fb_alu_ctrl #(.applicationType("IVERILOG"), .iverilogOptions("-I /Users/zhangyibo/riscvdesign/RISCVFirebird/Pipeline/rtl\n-y/Users/zhangyibo/riscvdesign/RISCVFirebird/Pipeline/rtl"), .CodeFile("/Users/zhangyibo/riscvdesign/RISCVFirebird/Pipeline/rtl/fb_alu_ctrl.v")) u_fb_alu_ctrl (
    .alu_op(aluop), .func7(inst[31:25]), .func3(inst[14:12]), .alu_control(u_fb_alu_ctrl_alu_control));
  t_data_sel #(.applicationType("IVERILOG"), .iverilogOptions("-I /Users/zhangyibo/riscvdesign/RISCVFirebird/Pipeline/rtl\n-y/Users/zhangyibo/riscvdesign/RISCVFirebird/Pipeline/rtl"), .CodeFile("/Users/zhangyibo/riscvdesign/RISCVFirebird/Pipeline/rtl/t_data_sel.v")) u_t_data_sel (
    .e00(e00), .e01(e01), .e11(e11), .d00(u_fb_status_reg_status), .d01(eddatareg_q), .d11(mem_d),
    .data(u_t_data_sel_data));
  fb_regfile #(.applicationType("IVERILOG"), .iverilogOptions("-I /Users/zhangyibo/riscvdesign/RISCVFirebird/Pipeline/rtl\n-y/Users/zhangyibo/riscvdesign/RISCVFirebird/Pipeline/rtl"), .CodeFile("/Users/zhangyibo/riscvdesign/RISCVFirebird/Pipeline/rtl/fb_regfile.v")) u_fb_regfile (
    .clk(clk), .reset(_0), .raddr1(inst[19:15]), .raddr2(inst[24:20]), .we(mwrw), .waddr(mwrd),
    .wdata(rbval), .rdata1(u_fb_regfile_rdata1), .rdata2(u_fb_regfile_rdata2));
  fb_imm_gen #(.applicationType("IVERILOG"), .iverilogOptions("-I /Users/zhangyibo/riscvdesign/RISCVFirebird/Pipeline/rtl\n-y/Users/zhangyibo/riscvdesign/RISCVFirebird/Pipeline/rtl"), .CodeFile("/Users/zhangyibo/riscvdesign/RISCVFirebird/Pipeline/rtl/fb_imm_gen.v")) u_fb_imm_gen (
    .inst(inst), .imm(immj));
  // IDEXReg idexreg_1: pin names not known; wires that end beside it: clk, _1, rst, alusrc, arsrc, mr, mw, bra, mtr, rw, pca1, u_fb_regfile_rdata1, u_fb_regfile_rdata2, immj, inst[19:15], inst[24:20], inst[11:7], u_fb_alu_ctrl_alu_control, dahulk, opc, iibrac, alusrc1, e2, mr1, mw1, bra1, mtr1, rw1, pca11, idexreg_1_p30, idexreg_1_p31, imm, rs11, rs22, rdd, aluct, iebrac, iepc
  MEMWBReg memwbreg_1 (
    .clk(clk), .we(_1), .m1(emmtr), .m2(emrw), .m3(u_t_data_sel_data), .m4(emalur), .m5(emrd), .w1(mwmtr),
    .w2(mwrw), .w3(memwbreg_1_w3), .w4(memwbreg_1_w4), .w5(mwrd));
  fb_ctrl_hazard_unit #(.applicationType("IVERILOG"), .iverilogOptions("-I /Users/zhangyibo/riscvdesign/RISCVFirebird/Pipeline/rtl\n-y/Users/zhangyibo/riscvdesign/RISCVFirebird/Pipeline/rtl"), .CodeFile("/Users/zhangyibo/riscvdesign/RISCVFirebird/Pipeline/rtl/fb_ctrl_hazard_unit.v")) u_fb_ctrl_hazard_unit (
    .pc(pc), .inst(ifinst), .branch(embra), .NF(NF), .ZF(ZF), .CF(CF), .VF(VF),
    .rs1_data(u_fb_regfile_rdata1), .jalr_en(jalren), .bra_pc(empc), .bra_imm(emimm), .i_bra_control(embrac),
    .jalr_imm(immj), .address_src(addsrc), .predict_pc(succpc), .predict_err_pc(errpc), .register_rst(rst),
    .pc_src(pcsrc), .lock(cthulk), .o_bra_control(obrac));
  fb_forwarding_unit #(.applicationType("IVERILOG"), .iverilogOptions("-I /Users/zhangyibo/riscvdesign/RISCVFirebird/Pipeline/rtl\n-y/Users/zhangyibo/riscvdesign/RISCVFirebird/Pipeline/rtl"), .CodeFile("/Users/zhangyibo/riscvdesign/RISCVFirebird/Pipeline/rtl/fb_forwarding_unit.v")) u_fb_forwarding_unit (
    .id_ex_register_rs1(rs11), .id_ex_register_rs2(rs22), .ex_mem_regwrite(emrw), .ex_mem_register_rd(emrd),
    .mem_wb_regwrite(mwrw), .mem_wb_register_rd(mwrd), .forward_a(fa), .forward_b(fb));
  fb_fwdmux fb_fwdmux_1 (.sel(fa), .\reg (idexreg_1_p30), .f10(emalur), .f01(rbval), .d(fb_fwdmux_1_d));
  fb_fwdmux fb_fwdmux_2 (.sel(fb), .\reg (idexreg_1_p31), .f10(emalur), .f01(rbval), .d(fb_fwdmux_2_d));
  Multiplexer #(.Bits(32)) multiplexer_4 (.sel(mwmtr), .in_0(memwbreg_1_w4), .in_1(memwbreg_1_w3), .out(rbval));
  Multiplexer #(.Bits(32)) multiplexer_5 (.sel(alusrc1), .in_0(fb_fwdmux_2_d), .in_1(imm), .out(multiplexer_5_out));
  fb_alu #(.applicationType("IVERILOG"), .iverilogOptions("-I /Users/zhangyibo/riscvdesign/RISCVFirebird/Pipeline/rtl\n-y/Users/zhangyibo/riscvdesign/RISCVFirebird/Pipeline/rtl"), .CodeFile("/Users/zhangyibo/riscvdesign/RISCVFirebird/Pipeline/rtl/fb_alu.v")) u_fb_alu (
    .alu_control(aluct), .op1(fb_fwdmux_1_d), .op2(multiplexer_5_out), .alu_res(u_fb_alu_alu_res),
    .csr(u_fb_alu_csr), .csr_write(u_fb_alu_csr_write));
  fb_csr #(.applicationType("IVERILOG"), .iverilogOptions("-I /Users/zhangyibo/riscvdesign/RISCVFirebird/Pipeline/rtl\n-y/Users/zhangyibo/riscvdesign/RISCVFirebird/Pipeline/rtl"), .CodeFile("/Users/zhangyibo/riscvdesign/RISCVFirebird/Pipeline/rtl/fb_csr.v")) u_fb_csr (
    .clk(clk), .we(u_fb_alu_csr_write), .csr(u_fb_alu_csr), .NF(NF), .ZF(ZF), .CF(CF), .VF(VF));
  Multiplexer #(.Bits(32)) multiplexer_6 (.sel(e2), .in_0(u_fb_alu_alu_res), .in_1(pca11), .out(multiplexer_6_out));
  EXMEMReg exmemreg_1 (
    .clk(clk), .we(_1), .rst(rst), .e1(mr1), .e2(mw1), .e3(bra1), .e4(mtr1), .e5(rw1),
    .e6(multiplexer_6_out), .e7(fb_fwdmux_2_d), .e8(rdd), .e10(imm), .e9(iepc), .e11(iebrac), .m1(emmr),
    .m2(emmw), .m3(embra), .m4(emmtr), .m5(emrw), .m6(emalur), .m7(emrs2d), .m8(emrd), .m9(empc),
    .m10(emimm), .m11(embrac));

  // Other names for the same wires on the sheet: rd[4:0] = inst[11:7]; rs1[4:0] = inst[19:15]; rs2[4:0] = inst[24:20];
  //   gcc = _1; gnd = _0

  // Notes on the sheet:
  //   _1: 默认使用的高电平, default 1
  //   _0: 低电平
endmodule
