// Digital circuit ROOTbak4-19test1.dig as structural Verilog
module ROOTbak4_19test1 (
  input  _1,
  input  _0,
  input  clk
);

  wire addsrc, alusrc, alusrc1, arsrc, av, bra, bra1, CF, clrstat, csrwe, cthulk, dahulk, e00, e01, e2, e11,
       embra, emmr, emmtr, emmw, emrw, iibrac, jalren, mr, mr1, mtr, mtr1, mw, mw1, mwmtr, mwrw, NF, opc,
       pca1, pcsrc, rst, rw, rw1, termen, u_t_f_decode_e10, VF, ZF;
  wire [1:0] aluop, fa, fb, mmudatasrc;
  wire [3:0] csr;
  wire [4:0] emrd, mwrd, rdd, rs11, rs22;
  wire [5:0] embrac, iebrac, obrac;
  wire [9:0] mmuadd;
  wire [15:0] keyboard_d;
  wire [18:0] aluct, aluctrl;
  wire [31:0] alures, d00data, d01data, emalur, emimm, empc, emrs2d, errpc, exinst, exrs2data, idexreg_1_p31,
       idexreg_1_p32, iepc, ifinst, imm, immj, inst, kbdata, mem_d, memdata, meminst, memwbreg_1_w3,
       memwbreg_1_w4, multiplexer_1_out, nextiradd, op1, op2, passalures, pc, pca11, pcn, rbval, rdata1,
       rdata2, succpc, termdata, wbinst;

  fb_mmu #(.applicationType("IVERILOG"), .iverilogOptions("-I /Users/zhangyibo/riscvdesign/RISCVFirebird/Pipeline/rtl\n-y/Users/zhangyibo/riscvdesign/RISCVFirebird/Pipeline/rtl"), .CodeFile("/Users/zhangyibo/riscvdesign/RISCVFirebird/Pipeline/rtl/fb_mmu.v")) u_fb_mmu (
    .in_add(emalur[10:0]), .data_src(mmudatasrc), .out_add(mmuadd), .clr_stat(clrstat));
  Keyboard keyboard (.C(clk), .en(_1), .D(keyboard_d), .av(av));
  Multiplexer #(.Bits(32)) multiplexer_1 (.sel(addsrc), .in_0(succpc), .in_1(errpc), .out(multiplexer_1_out));
  BitExtender #(.inputBits(16), .outputBits(32)) bitextender_1 (.in(keyboard_d), .out(kbdata));
  t_f_decode #(.applicationType("IVERILOG"), .CodeFile("/Users/zhangyibo/riscvdesign/RISCVFirebird/Pipeline/rtl/t_f_decode.v")) u_t_f_decode (
    .c(mmudatasrc), .e00(e00), .e01(e01), .e10(u_t_f_decode_e10), .e11(e11));
  Multiplexer #(.Bits(32)) multiplexer_2 (.sel(pcsrc), .in_0(pcn), .in_1(multiplexer_1_out), .out(nextiradd));
  Multiplexer #(.Bits(32)) multiplexer_3 (.sel(u_t_f_decode_e10), .in_0(kbdata), .in_1(emrs2d), .out(termdata));
  IF if_1 (.clk(clk), .pw(dahulk), .rs(_0), .ad(nextiradd), .clr(cthulk), .ir(ifinst), .pc(pc));
  or or_1 (termen, u_t_f_decode_e10, av);
  Add #(.Bits(32)) adderpc (.a(pc), .b(32'h1), .c_i(_0), .s(pcn), .c_o(_0));
  // Probe on inst[19:15]
  LED led_1 (.in(emrw));
  fb_status_reg #(.applicationType("IVERILOG"), .iverilogOptions("-I /Users/zhangyibo/riscvdesign/RISCVFirebird/Pipeline/rtl\n-y/Users/zhangyibo/riscvdesign/RISCVFirebird/Pipeline/rtl"), .CodeFile("/Users/zhangyibo/riscvdesign/RISCVFirebird/Pipeline/rtl/fb_status_reg.v")) u_fb_status_reg (
    .clk(clk), .clr(clrstat), .av(av), .status(d00data));
  Register #(.Bits(32)) eddatareg (.D(kbdata), .C(clk), .en(av), .Q(d01data));
  Terminal terminal (.D(termdata), .C(clk), .en(termen));
  RAMDualPort #(.AddrBits(10), .Bits(32)) mem (.A(mmuadd), .Din(emrs2d), .str(emmw), .C(clk), .ld(emmr), .D(mem_d));
  LED led_2 (.in(dahulk));
  // IFIDReg ifidreg_1: pin names not known; wires that end beside it: clk, dahulk, _1, rst, pc, pcn, ifinst, obrac, opc, inst, pca1, iibrac
  // Probe on inst[24:20]
  // Probe on rdd
  fb_hazard_detection_unit #(.applicationType("IVERILOG"), .iverilogOptions("-I /Users/zhangyibo/riscvdesign/RISCVFirebird/Pipeline/rtl\n-y/Users/zhangyibo/riscvdesign/RISCVFirebird/Pipeline/rtl"), .CodeFile("/Users/zhangyibo/riscvdesign/RISCVFirebird/Pipeline/rtl/fb_hazard_detection_unit.v")) u_fb_hazard_detection_unit (
    .id_ex_memread(mr1), .id_ex_register_rd(rdd), .inst(inst[24:15]), .lock(dahulk));
  fb_cu #(.applicationType("IVERILOG"), .iverilogOptions("-I /Users/zhangyibo/riscvdesign/RISCVFirebird/Pipeline/rtl\n-y/Users/zhangyibo/riscvdesign/RISCVFirebird/Pipeline/rtl"), .CodeFile("/Users/zhangyibo/riscvdesign/RISCVFirebird/Pipeline/rtl/fb_cu.v")) u_fb_cu (
    .opcode(inst[6:0]), .alu_op(aluop), .alu_src(alusrc), .alu_res_src(arsrc), .mem_read(mr), .mem_write(mw),
    .branch(bra), .mem_to_reg(mtr), .reg_write(rw), .jalr_en(jalren));
  LED led_3 (.in(clk));
  LED led_4 (.in(clk));
  LED led_5 (.in(clk));
  LED led_6 (.in(clk));
  LED led_7 (.in(clk));
  fb_regfile #(.applicationType("IVERILOG"), .iverilogOptions("-I /Users/zhangyibo/riscvdesign/RISCVFirebird/Pipeline/rtl\n-y/Users/zhangyibo/riscvdesign/RISCVFirebird/Pipeline/rtl"), .CodeFile("/Users/zhangyibo/riscvdesign/RISCVFirebird/Pipeline/rtl/fb_regfile.v")) u_fb_regfile (
    .clk(clk), .reset(_0), .raddr1(inst[19:15]), .raddr2(inst[24:20]), .we(mwrw), .waddr(mwrd),
    .wdata(rbval), .rdata1(rdata1), .rdata2(rdata2));
  fb_alu_ctrl #(.applicationType("IVERILOG"), .iverilogOptions("-I /Users/zhangyibo/riscvdesign/RISCVFirebird/Pipeline/rtl\n-y/Users/zhangyibo/riscvdesign/RISCVFirebird/Pipeline/rtl"), .CodeFile("/Users/zhangyibo/riscvdesign/RISCVFirebird/Pipeline/rtl/fb_alu_ctrl.v")) u_fb_alu_ctrl (
    .alu_op(aluop), .func7(inst[31:25]), .func3(inst[14:12]), .alu_control(aluctrl));
  t_data_sel #(.applicationType("IVERILOG"), .iverilogOptions("-I /Users/zhangyibo/riscvdesign/RISCVFirebird/Pipeline/rtl\n-y/Users/zhangyibo/riscvdesign/RISCVFirebird/Pipeline/rtl"), .CodeFile("/Users/zhangyibo/riscvdesign/RISCVFirebird/Pipeline/rtl/t_data_sel.v")) u_t_data_sel (
    .e00(e00), .e01(e01), .e11(e11), .d00(d00data), .d01(d01data), .d11(mem_d), .data(memdata));
  // Probe on emalur
  LED led_8 (.in(av));
  LED led_9 (.in(_1));
  fb_imm_gen #(.applicationType("IVERILOG"), .iverilogOptions("-I /Users/zhangyibo/riscvdesign/RISCVFirebird/Pipeline/rtl\n-y/Users/zhangyibo/riscvdesign/RISCVFirebird/Pipeline/rtl"), .CodeFile("/Users/zhangyibo/riscvdesign/RISCVFirebird/Pipeline/rtl/fb_imm_gen.v")) u_fb_imm_gen (
    .inst(inst), .imm(immj));
  LED led_10 (.in(rst));
  // Probe on mmudatasrc
  LED led_11 (.in(clrstat));
  LED led_12 (.in(termen));
  // Probe on memdata
  LED led_13 (.in(av));
  LED led_14 (.in(emmr));
  // Probe on mmuadd
  // Probe on d01data
  // Probe on kbdata
  // Probe on termdata
  LED led_15 (.in(NF));
  // Probe on pc
  LED led_16 (.in(jalren));
  LED led_17 (.in(embra));
  // Probe on embrac
  LED led_18 (.in(addsrc));
  // IDEXReg idexreg_1: pin names not known; wires that end beside it: clk, _1, rst, alusrc, arsrc, mr, mw, bra, mtr, rw, pca1, rdata1, rdata2, immj, inst[19:15], inst[24:20], inst[11:7], aluctrl, dahulk, opc, iibrac, inst, alusrc1, e2, mr1, mw1, bra1, mtr1, rw1, pca11, idexreg_1_p31, idexreg_1_p32, imm, rs11, rs22, rdd, aluct, iebrac, iepc, exinst
  MEMWBReg memwbreg_1 (
    .clk(clk), .we(_1), .m1(emmtr), .m2(emrw), .m3(memdata), .m4(emalur), .m5(emrd), .m6(meminst),
    .w1(mwmtr), .w2(mwrw), .w3(memwbreg_1_w3), .w4(memwbreg_1_w4), .w5(mwrd), .w6(wbinst));
  // Probe on meminst
  // Probe on emrs2d
  // Probe on d00data
  // Probe on errpc
  // Probe on obrac
  LED led_19 (.in(emmw));
  LED led_20 (.in(ZF));
  // Probe on rdata1
  // Probe on empc
  LED led_21 (.in(pcsrc));
  fb_ctrl_hazard_unit #(.applicationType("IVERILOG"), .iverilogOptions("-I /Users/zhangyibo/riscvdesign/RISCVFirebird/Pipeline/rtl\n-y/Users/zhangyibo/riscvdesign/RISCVFirebird/Pipeline/rtl"), .CodeFile("/Users/zhangyibo/riscvdesign/RISCVFirebird/Pipeline/rtl/fb_ctrl_hazard_unit.v")) u_fb_ctrl_hazard_unit (
    .pc(pc), .inst(ifinst), .branch(embra), .NF(NF), .ZF(ZF), .CF(CF), .VF(VF), .rs1_data(rdata1),
    .jalr_en(jalren), .bra_pc(empc), .bra_imm(emimm), .i_bra_control(embrac), .jalr_imm(immj),
    .address_src(addsrc), .predict_pc(succpc), .predict_err_pc(errpc), .register_rst(rst), .pc_src(pcsrc),
    .lock(cthulk), .o_bra_control(obrac));
  fb_forwarding_unit #(.applicationType("IVERILOG"), .iverilogOptions("-I /Users/zhangyibo/riscvdesign/RISCVFirebird/Pipeline/rtl\n-y/Users/zhangyibo/riscvdesign/RISCVFirebird/Pipeline/rtl"), .CodeFile("/Users/zhangyibo/riscvdesign/RISCVFirebird/Pipeline/rtl/fb_forwarding_unit.v")) u_fb_forwarding_unit (
    .id_ex_register_rs1(rs11), .id_ex_register_rs2(rs22), .ex_mem_regwrite(emrw), .ex_mem_register_rd(emrd),
    .mem_wb_regwrite(mwrw), .mem_wb_register_rd(mwrd), .forward_a(fa), .forward_b(fb));
  LED led_22 (.in(clrstat));
  LED led_23 (.in(av));
  fb_fwdmux fb_fwdmux_1 (.sel(fa), .\reg (idexreg_1_p31), .f10(emalur), .f01(rbval), .d(op1));
  fb_fwdmux fb_fwdmux_2 (.sel(fb), .\reg (idexreg_1_p32), .f10(emalur), .f01(rbval), .d(exrs2data));
  // Probe on ifinst
  Multiplexer #(.Bits(32)) multiplexer_4 (.sel(mwmtr), .in_0(memwbreg_1_w4), .in_1(memwbreg_1_w3), .out(rbval));
  LED led_24 (.in(CF));
  // Probe on immj
  // Probe on emimm
  LED led_25 (.in(rst));
  Multiplexer #(.Bits(32)) multiplexer_5 (.sel(alusrc1), .in_0(exrs2data), .in_1(imm), .out(op2));
  // Probe on succpc
  fb_alu #(.applicationType("IVERILOG"), .iverilogOptions("-I /Users/zhangyibo/riscvdesign/RISCVFirebird/Pipeline/rtl\n-y/Users/zhangyibo/riscvdesign/RISCVFirebird/Pipeline/rtl"), .CodeFile("/Users/zhangyibo/riscvdesign/RISCVFirebird/Pipeline/rtl/fb_alu.v")) u_fb_alu (
    .alu_control(aluct), .op1(op1), .op2(op2), .alu_res(alures), .csr(csr), .csr_write(csrwe));
  LED led_26 (.in(VF));
  LED led_27 (.in(cthulk));
  LED led_28 (.in(clk));
  // Probe on mwrd
  fb_csr #(.applicationType("IVERILOG"), .iverilogOptions("-I /Users/zhangyibo/riscvdesign/RISCVFirebird/Pipeline/rtl\n-y/Users/zhangyibo/riscvdesign/RISCVFirebird/Pipeline/rtl"), .CodeFile("/Users/zhangyibo/riscvdesign/RISCVFirebird/Pipeline/rtl/fb_csr.v")) u_fb_csr (
    .clk(clk), .we(csrwe), .csr(csr), .NF(NF), .ZF(ZF), .CF(CF), .VF(VF));
  Multiplexer #(.Bits(32)) multiplexer_6 (.sel(e2), .in_0(alures), .in_1(pca11), .out(passalures));
  // Probe on rs11
  LED led_29 (.in(emrw));
  LED led_30 (.in(mwrw));
  // Probe on fa
  EXMEMReg exmemreg_1 (
    .clk(clk), .we(_1), .rst(rst), .e1(mr1), .e2(mw1), .e3(bra1), .e4(mtr1), .e5(rw1), .e6(passalures),
    .e7(exrs2data), .e8(rdd), .e10(imm), .e9(iepc), .e11(iebrac), .e12(exinst), .m1(emmr), .m2(emmw),
    .m3(embra), .m4(emmtr), .m5(emrw), .m6(emalur), .m7(emrs2d), .m8(emrd), .m9(empc), .m10(emimm),
    .m11(embrac), .m12(meminst));
  // Probe on rs22
  // Probe on emrd
  // Probe on mwrd
  // Probe on fb
  LED led_31 (.in(mwmtr));
  // Probe on rbval
  // Probe on wbinst
  LED led_32 (.in(mwrw));
  LED led_33 (.in(clk));
  LED led_34 (.in(clk));
  LED led_35 (.in(clk));
  // Probe on pc
  LED led_36 (.in(alusrc));
  // Probe on rdata1
  // Probe on immj
  LED led_37 (.in(alusrc1));
  // Probe on fa
  LED led_38 (.in(csrwe));
  LED led_39 (.in(dahulk));
  LED led_40 (.in(dahulk));
  LED led_41 (.in(bra));
  // Probe on rdata2
  LED led_42 (.in(dahulk));
  // Probe on alures
  // Probe on passalures
  // Probe on pcn
  LED led_43 (.in(arsrc));
  LED led_44 (.in(e2));
  // Probe on fb
  LED led_45 (.in(cthulk));
  LED led_46 (.in(rst));
  LED led_47 (.in(mtr));
  LED led_48 (.in(rst));
  LED led_49 (.in(mr));
  // Probe on inst[19:15]
  // Probe on aluctrl
  // Probe on aluct
  // Probe on op1
  // Probe on csr
  // Probe on exrs2data
  // Probe on nextiradd
  // Probe on ifinst
  LED led_50 (.in(rw));
  // Probe on inst[24:20]
  // Probe on inst
  LED led_51 (.in(mw));
  // Probe on exinst
  // Probe on inst[11:7]
  // Probe on op2

  // Other names for the same wires on the sheet: rd[4:0] = inst[11:7]; rs1[4:0] = inst[19:15]; rs2[4:0] = inst[24:20];
  //   gcc = _1; gnd = _0

  // Notes on the sheet:
  //   _1: 默认使用的高电平, default 1
  //   _0: 低电平
  //   clk: Hz: 100
  //   数据冒险停顿单元
  //   输入信号
  //   IDrs1寄存器号
  //   EX阶段指令是否存储器读
  //   输出停顿信号
  //   停顿信号
  //   IDrs2寄存器号
  //   EX阶段rd寄存器
  //   MEM（访存）
  //   MMU
  //   状态寄存器
  //   数据寄存器
  //   键盘
  //   终端
  //   输出信号
  //   时钟
  //   EX的运算结果
  //   MMU产生的数据源
  //   MEM阶段得到的结果
  //   当前指令
  //   清空ID/EX寄存器
  //   读后擦除
  //   使能
  //   MMU产生的数据地址
  //   键盘输入数据
  //   存储器读
  //   寄存器数据
  //   终端输入数据
  //   控制冒险单元（跳转、分支）
  //   标志状态
  //   是否为负数
  //   jal（IF阶段完成并前递）
  //   jalr（停顿一周期并前递）
  //   jalr停顿完成
  //   branch（分支指令的预测与判断）
  //   分支执行完成
  //   分支指令控制信号
  //   输出信号 决定下一指令地址
  //   使用预测错误地址
  //   寄存器2数值
  //   状态值
  //   当前pc
  //   预测错误pc
  //   分支指令控制信号,在MEM阶段这会作为单元的输入
  //   存储器写
  //   rs1寄存器数据
  //   原取分支指令时pc
  //   使用控制冒险单元地址
  //   状态寄存器读后清除信号
  //   当前有数据输入
  //   是否为0
  //   {beq_ins, bne_ins, blt_ins, bge_ins, bltu_ins, bgeu_ins}
  //   指令
  //   进位
  //   jalr指令立即数
  //   原分支指令立即数
  //   预测错误清空流水线
  //   预测pc或前递的pc
  //   溢出
  //   jalr周期停顿
  //   数据冒险前递单元
  //   WB（写回）
  //   写回寄存器号
  //   ID/EXrs1寄存器号
  //   EX/MEM阶段指令是否写寄存器
  //   MEM/WB阶段指令是否写寄存器
  //   输出前递信号
  //   op1数据选择信号
  //   写回寄存器数据来源
  //   ID/EXrs2寄存器号
  //   EX/MEMrd寄存器号
  //   MEM/WBrd寄存器号
  //   op2数据选择信号
  //   写回寄存器数值
  //   寄存器写使能
  //   IF（取指）
  //   ID（译码、读寄存器）
  //   EX（执行）
  //   alu操作数来源
  //   rs1数值
  //   立即数生成
  //   标志位写
  //   向后传递的运算结果
  //   锁存
  //   锁存IF/ID寄存器
  //   是否分支指令
  //   rs2数值
  //   锁存ID/EX寄存器
  //   运算结果
  //   下一pc
  //   J类型指令使用
  //   alu结果来源
  //   jalr停顿
  //   清空IF/ID寄存器
  //   rs1号
  //   alu控制信号
  //   {op_mul, op_mulh, op_mulhsu, op_mulhu,
  //    op_div, op_divu, op_rem, op_remu,
  //    op_add, op_sub, op_sll, op_slt, op_sltu, 
  //    op_xor, op_srl, op_sra, op_or, op_and, op_branch};
  //   alu控制信号
  //   操作数1
  //   标志位
  //   下一取指地址
  //   寄存器写
  //   rs2号
  //   rd号
  //   操作数2
endmodule
