// Digital circuit fb_fwdmux.dig as structural Verilog
module fb_fwdmux (
  input  [1:0] sel,
  input  [31:0] \reg ,
  input  [31:0] f10,
  input  [31:0] f01,
  output [31:0] d
);

  fb_fwdmux #(.applicationType("IVERILOG"), .iverilogOptions("-I /Users/zhangyibo/riscvdesign/RISCVFirebird/Pipeline/rtl\n-y/Users/zhangyibo/riscvdesign/RISCVFirebird/Pipeline/rtl"), .CodeFile("/Users/zhangyibo/riscvdesign/RISCVFirebird/Pipeline/rtl/fb_fwdmux.v")) u_fb_fwdmux (
    .sel(sel), .reg_data(\reg ), .forward_10_data(f10), .forward_01_data(f01), .d(d));

  // Notes on the sheet:
  //   sel: 选择
  //   d: 选择输出
endmodule
