// Digital circuit firebird_single_design.dig as structural Verilog
module firebird_single_design (
  input  in_1,
  input  clk,
  input  clk_2,
  input  clk_3,
  input  in_5
);

  wire alusrc, and_1_out, memread, memtoreg, memwrite, NU, regwrite, u_firebird_alu_res_zero,
       u_firebird_cu_branch;
  wire [1:0] u_firebird_cu_alu_op;
  wire [3:0] u_firebird_alu_ctrl_alu_ctrl_signal;
  wire [7:0] u_firebird_pc_out_address;
  wire [31:0] add_1_s, add_2_s, alures, instmem_d, multiplexer_1_out, multiplexer_2_out, multiplexer_3_out,
       ramdualport_1_d, u_firebird_imm_gen_imm, u_firebird_regfile_rdata1, u_firebird_regfile_rdata2;
  wire [31:8] u_firebird_pc_out_address_2;

  firebird_pc #(.applicationType("IVERILOG"), .iverilogOptions("-y /Users/zhangyibo/riscvdesign/RISCVFirebird/SingleCycle/rtl/ -I /Users/zhangyibo/riscvdesign/RISCVFirebird/SingleCycle/rtl/"), .CodeFile("/Users/zhangyibo/riscvdesign/RISCVFirebird/SingleCycle/rtl/firebird_pc.v")) u_firebird_pc (
    .clk(clk), .pc_reset(in_1), .new_address(multiplexer_2_out),
    .out_address({u_firebird_pc_out_address_2, u_firebird_pc_out_address}));
  Add #(.Bits(32)) add_1 (
    .a(32'h4), .b({u_firebird_pc_out_address_2, u_firebird_pc_out_address}), .c_i(NU), .s(add_1_s), .c_o(NU));
  // Probe on {u_firebird_pc_out_address_2, u_firebird_pc_out_address}
  ROM #(.AddrBits(8), .Bits(32)) instmem (.A(u_firebird_pc_out_address), .sel(1'b1), .D(instmem_d));
  // Probe on instmem_d
  firebird_cu #(.applicationType("IVERILOG"), .iverilogOptions("-y /Users/zhangyibo/riscvdesign/RISCVFirebird/SingleCycle/rtl/ -I /Users/zhangyibo/riscvdesign/RISCVFirebird/SingleCycle/rtl/"), .CodeFile("/Users/zhangyibo/riscvdesign/RISCVFirebird/SingleCycle/rtl/firebird_cu.v")) u_firebird_cu (
    .opcode(instmem_d[6:0]), .branch(u_firebird_cu_branch), .mem_read(memread), .mem_to_reg(memtoreg),
    .alu_op(u_firebird_cu_alu_op), .mem_write(memwrite), .alu_src(alusrc), .reg_write(regwrite));
  firebird_regfile #(.applicationType("IVERILOG"), .iverilogOptions("-y /Users/zhangyibo/riscvdesign/RISCVFirebird/SingleCycle/rtl/ -I /Users/zhangyibo/riscvdesign/RISCVFirebird/SingleCycle/rtl/"), .CodeFile("/Users/zhangyibo/riscvdesign/RISCVFirebird/SingleCycle/rtl/firebird_regfile.v")) u_firebird_regfile (
    .clk(clk_3), .reset(in_5), .raddr1(instmem_d[19:15]), .raddr2(instmem_d[24:20]), .we(regwrite),
    .waddr(instmem_d[11:7]), .wdata(multiplexer_3_out), .rdata1(u_firebird_regfile_rdata1),
    .rdata2(u_firebird_regfile_rdata2));
  firebird_imm_gen #(.applicationType("IVERILOG"), .iverilogOptions("-y /Users/zhangyibo/riscvdesign/RISCVFirebird/SingleCycle/rtl/ -I /Users/zhangyibo/riscvdesign/RISCVFirebird/SingleCycle/rtl/"), .CodeFile("/Users/zhangyibo/riscvdesign/RISCVFirebird/SingleCycle/rtl/firebird_imm_gen.v")) u_firebird_imm_gen (
    .inst(instmem_d), .imm(u_firebird_imm_gen_imm));
  Add #(.Bits(32)) add_2 (
    .a({u_firebird_pc_out_address_2, u_firebird_pc_out_address}), .b(u_firebird_imm_gen_imm), .c_i(NU),
    .s(add_2_s), .c_o(NU));
  Multiplexer #(.Bits(32)) multiplexer_1 (
    .sel(alusrc), .in_0(u_firebird_regfile_rdata2), .in_1(u_firebird_imm_gen_imm), .out(multiplexer_1_out));
  Multiplexer #(.Bits(32)) multiplexer_2 (.sel(and_1_out), .in_0(add_1_s), .in_1(add_2_s), .out(multiplexer_2_out));
  and and_1 (and_1_out, u_firebird_cu_branch, u_firebird_alu_res_zero);
  firebird_alu #(.applicationType("IVERILOG"), .iverilogOptions("-y /Users/zhangyibo/riscvdesign/RISCVFirebird/SingleCycle/rtl/ -I /Users/zhangyibo/riscvdesign/RISCVFirebird/SingleCycle/rtl/"), .CodeFile("/Users/zhangyibo/riscvdesign/RISCVFirebird/SingleCycle/rtl/firebird_alu.v")) u_firebird_alu (
    .alu_data1(u_firebird_regfile_rdata1), .alu_data2(multiplexer_1_out),
    .alu_ctrl_signal(u_firebird_alu_ctrl_alu_ctrl_signal), .alu_result(alures),
    .res_zero(u_firebird_alu_res_zero));
  firebird_alu_ctrl #(.applicationType("IVERILOG"), .iverilogOptions("-y /Users/zhangyibo/riscvdesign/RISCVFirebird/SingleCycle/rtl/ -I /Users/zhangyibo/riscvdesign/RISCVFirebird/SingleCycle/rtl/"), .CodeFile("/Users/zhangyibo/riscvdesign/RISCVFirebird/SingleCycle/rtl/firebird_alu_ctrl.v")) u_firebird_alu_ctrl (
    .inst({instmem_d[14:12], instmem_d[30]}), .alu_op(u_firebird_cu_alu_op),
    .alu_ctrl_signal(u_firebird_alu_ctrl_alu_ctrl_signal));
  // Probe on u_firebird_regfile_rdata1
  // Probe on multiplexer_1_out
  // Probe on alures
  // Probe on u_firebird_regfile_rdata2
  // Probe on multiplexer_3_out
  RAMDualPort #(.AddrBits(8), .Bits(32)) ramdualport_1 (
    .A(alures[7:0]), .Din(u_firebird_regfile_rdata2), .str(memwrite), .C(clk_2), .ld(memread),
    .D(ramdualport_1_d));
  Multiplexer #(.Bits(32)) multiplexer_3 (
    .sel(memtoreg), .in_0(alures), .in_1(ramdualport_1_d), .out(multiplexer_3_out));
  // also tied to GND on the sheet: NU

  // Other names for the same wires on the sheet: C = clk; memclk = clk_2; regclk = clk_3

  // Notes on the sheet:
  //   clk_2: Hz: 2
  //   clk_3: Hz: 2
  //   contents of instmem (hex, n*v repeats v):
  //   28303,0,0,0,400333,0,0,0,6280a3,0,0,0,128383
endmodule
